// Logisim project td1.circ as structural Verilog: 8 circuits, main circuit XOR
module XOR (
  input  in_1,
  input  in_2,
  output out_3
);

  wire and_1_out, not_1_out, or_1_out;

  and and_1 (and_1_out, in_1, in_2);
  not not_1 (not_1_out, and_1_out);
  or or_1 (or_1_out, in_2, in_1);
  and and_2 (out_3, not_1_out, or_1_out);

  // Notes on the sheet:
  //   XOR GATE
endmodule

module _1_bit_adder (
  input  A,
  input  B,
  input  C_in,
  output S,
  output C_out
);

  wire and_1_out, and_2_out, and_3_out, or_1_out, xor_1_out;

  xor xor_1 (xor_1_out, A, B);
  and and_1 (and_1_out, A, B);
  xor xor_2 (S, xor_1_out, C_in);
  and and_2 (and_2_out, A, C_in);
  and and_3 (and_3_out, C_in, B);
  or or_1 (or_1_out, and_2_out, and_3_out);
  or or_2 (C_out, or_1_out, and_1_out);
endmodule

module _8_bit_adder (
  input  Ab0,
  input  Ab1,
  input  Ab2,
  input  Ab3,
  input  Ab4,
  input  Ab5,
  input  Ab6,
  input  Ab7,
  input  C_in,
  input  Bb0,
  input  Bb1,
  input  Bb2,
  input  Bb3,
  input  Bb4,
  input  Bb5,
  input  Bb6,
  input  Bb7,
  output C_out,
  output Sb0,
  output Sb1,
  output Sb2,
  output Sb3,
  output Sb4,
  output Sb5,
  output Sb6,
  output Sb7
);

  wire n1_bit_adder_1_c_out, n1_bit_adder_2_c_out, n1_bit_adder_3_c_out, n1_bit_adder_4_c_out,
       n1_bit_adder_5_c_out, n1_bit_adder_6_c_out, n1_bit_adder_7_c_out;

  _1_bit_adder u_1_bit_adder_1 (.A(Ab0), .B(Bb0), .C_in(C_in), .S(Sb0), .C_out(n1_bit_adder_1_c_out));
  _1_bit_adder u_1_bit_adder_2 (.A(Ab1), .B(Bb1), .C_in(n1_bit_adder_1_c_out), .S(Sb1), .C_out(n1_bit_adder_2_c_out));
  _1_bit_adder u_1_bit_adder_3 (.A(Ab2), .B(Bb2), .C_in(n1_bit_adder_2_c_out), .S(Sb2), .C_out(n1_bit_adder_3_c_out));
  _1_bit_adder u_1_bit_adder_4 (.A(Ab3), .B(Bb3), .C_in(n1_bit_adder_3_c_out), .S(Sb3), .C_out(n1_bit_adder_4_c_out));
  _1_bit_adder u_1_bit_adder_5 (.A(Ab4), .B(Bb4), .C_in(n1_bit_adder_4_c_out), .S(Sb4), .C_out(n1_bit_adder_5_c_out));
  _1_bit_adder u_1_bit_adder_6 (.A(Ab5), .B(Bb5), .C_in(n1_bit_adder_5_c_out), .S(Sb5), .C_out(n1_bit_adder_6_c_out));
  _1_bit_adder u_1_bit_adder_7 (.A(Ab6), .B(Bb6), .C_in(n1_bit_adder_6_c_out), .S(Sb6), .C_out(n1_bit_adder_7_c_out));
  _1_bit_adder u_1_bit_adder_8 (.A(Ab7), .B(Bb7), .C_in(n1_bit_adder_7_c_out), .S(Sb7), .C_out(C_out));
endmodule

module Test (
  input  [7:0] in_1,
  input  [7:0] in_2,
  input  in_3,
  output out_4,
  output [7:0] out_5
);

  _8_bit_adder u_8_bit_adder_1 (
    .C_in(in_3), .C_out(out_4), .Ab0(in_1[0]), .Ab1(in_1[1]), .Ab2(in_1[2]), .Ab3(in_1[3]), .Ab4(in_1[4]),
    .Ab5(in_1[5]), .Ab6(in_1[6]), .Ab7(in_1[7]), .Bb0(in_2[0]), .Sb0(out_5[0]), .Bb1(in_2[1]),
    .Sb1(out_5[1]), .Bb2(in_2[2]), .Sb2(out_5[2]), .Bb3(in_2[3]), .Sb3(out_5[3]), .Bb4(in_2[4]),
    .Sb4(out_5[4]), .Bb5(in_2[5]), .Sb5(out_5[5]), .Bb6(in_2[6]), .Sb6(out_5[6]), .Bb7(in_2[7]),
    .Sb7(out_5[7]));
endmodule

module _8bit2Comp (
  input  [7:0] A,
  output C_out,
  output [7:0] neg_A
);

  wire [7:0] not_1_out;

  assign not_1_out = ~A;  // NOT_Gate not_1, 8 bits wide
  _8_bit_adder u_8_bit_adder_1 (
    .C_in(1'b0), .C_out(C_out), .Ab0(1'b1), .Ab1(1'b0), .Ab2(1'b0), .Ab3(1'b0), .Ab4(1'b0), .Ab5(1'b0),
    .Ab6(1'b0), .Ab7(1'b0), .Bb0(not_1_out[0]), .Sb0(neg_A[0]), .Bb1(not_1_out[1]), .Sb1(neg_A[1]),
    .Bb2(not_1_out[2]), .Sb2(neg_A[2]), .Bb3(not_1_out[3]), .Sb3(neg_A[3]), .Bb4(not_1_out[4]),
    .Sb4(neg_A[4]), .Bb5(not_1_out[5]), .Sb5(neg_A[5]), .Bb6(not_1_out[6]), .Sb6(neg_A[6]),
    .Bb7(not_1_out[7]), .Sb7(neg_A[7]));
endmodule

module Test_2 (
  input  [7:0] in_1,
  input  in_2,
  input  [7:0] in_3,
  input  C_in,
  output C_out,
  output [7:0] out_6
);

  wire [7:0] multiplexer_1_out, n8bit2comp_1_neg_a;

  _8bit2Comp u_8bit2comp_1 (.A(in_1), .neg_A(n8bit2comp_1_neg_a));  // open: C_out
  _8_bit_adder u_8_bit_adder_1 (
    .C_in(C_in), .C_out(C_out), .Ab0(in_3[0]), .Ab1(in_3[1]), .Ab2(in_3[2]), .Ab3(in_3[3]), .Ab4(in_3[4]),
    .Ab5(in_3[5]), .Ab6(in_3[6]), .Ab7(in_3[7]), .Bb0(multiplexer_1_out[0]), .Sb0(out_6[0]),
    .Bb1(multiplexer_1_out[1]), .Sb1(out_6[1]), .Bb2(multiplexer_1_out[2]), .Sb2(out_6[2]),
    .Bb3(multiplexer_1_out[3]), .Sb3(out_6[3]), .Bb4(multiplexer_1_out[4]), .Sb4(out_6[4]),
    .Bb5(multiplexer_1_out[5]), .Sb5(out_6[5]), .Bb6(multiplexer_1_out[6]), .Sb6(out_6[6]),
    .Bb7(multiplexer_1_out[7]), .Sb7(out_6[7]));
  Multiplexer #(.width(8), .disabled(0), .enable("false")) multiplexer_1 (
    .in0(in_1), .in1(n8bit2comp_1_neg_a), .out(multiplexer_1_out), .sel(in_2));
endmodule

module True_AddSub (
  input  [7:0] in_1,
  input  [7:0] in_2,
  input  C_in,
  output C_out,
  output [7:0] out_5
);

  wire [7:0] n8xor_1_out_3;

  _8xor u_8xor_1 (.in_1(in_1), .C_in(C_in), .out_3(n8xor_1_out_3));
  _8_bit_adder u_8_bit_adder_1 (
    .C_in(C_in), .C_out(C_out), .Ab0(in_2[0]), .Ab1(in_2[1]), .Ab2(in_2[2]), .Ab3(in_2[3]), .Ab4(in_2[4]),
    .Ab5(in_2[5]), .Ab6(in_2[6]), .Ab7(in_2[7]), .Bb0(n8xor_1_out_3[0]), .Sb0(out_5[0]),
    .Bb1(n8xor_1_out_3[1]), .Sb1(out_5[1]), .Bb2(n8xor_1_out_3[2]), .Sb2(out_5[2]), .Bb3(n8xor_1_out_3[3]),
    .Sb3(out_5[3]), .Bb4(n8xor_1_out_3[4]), .Sb4(out_5[4]), .Bb5(n8xor_1_out_3[5]), .Sb5(out_5[5]),
    .Bb6(n8xor_1_out_3[6]), .Sb6(out_5[6]), .Bb7(n8xor_1_out_3[7]), .Sb7(out_5[7]));
endmodule

module _8xor (
  input  [7:0] in_1,
  input  C_in,
  output [7:0] out_3
);

  xor xor_1 (out_3[0], in_1[0], C_in);
  xor xor_2 (out_3[1], in_1[1], C_in);
  xor xor_3 (out_3[2], in_1[2], C_in);
  xor xor_4 (out_3[3], in_1[3], C_in);
  xor xor_5 (out_3[4], in_1[4], C_in);
  xor xor_6 (out_3[5], in_1[5], C_in);
  xor xor_7 (out_3[6], in_1[6], C_in);
  xor xor_8 (out_3[7], in_1[7], C_in);
endmodule
