// Logisim project tpMembackup.circ as structural Verilog: 16 circuits, main circuit Registre 1 bit
module Registre_1_bit (
  input  e,
  input  ce,
  input  reset,
  input  ck,
  output out_5
);

  wire multiplexer_1_out, multiplexer_2_out, multiplexer_3_out, not_1_out;

  Multiplexer #(.enable("false")) multiplexer_1 (.in0(out_5), .in1(e), .out(multiplexer_1_out), .sel(ce));
  not not_1 (not_1_out, reset);
  Multiplexer #(.enable("false")) multiplexer_2 (
    .in0(multiplexer_1_out), .in1(not_1_out), .out(multiplexer_2_out), .sel(reset));
  Multiplexer #(.disabled(0), .enable("false")) multiplexer_3 (
    .in0(multiplexer_2_out), .in1(multiplexer_3_out), .out(multiplexer_3_out), .sel(ck));
  Multiplexer #(.enable("false")) multiplexer_4 (.in0(out_5), .in1(multiplexer_3_out), .out(out_5), .sel(ck));
endmodule

module flip_reset (
  output out_1
);

  wire ck_out, multiplexer_1_out, undriven;

  Multiplexer #(.disabled(0), .enable("false")) multiplexer_1 (
    .in0(multiplexer_1_out), .in1(undriven), .out(multiplexer_1_out), .sel(ck_out));
  Clock #(.highDuration(500), .lowDuration(500)) ck (.out(ck_out));
  Multiplexer #(.disabled(0), .enable("false")) multiplexer_2 (
    .in0(multiplexer_1_out), .in1(out_1), .out(out_1), .sel(ck_out));
endmodule

module name (
  input  in_1,
  input  in_2,
  input  in_3,
  output out_4
);

  wire clock_1_out;

  Clock clock_1 (.out(clock_1_out));
  Registre_1_bit registre_1_bit_1 (.e(in_1), .out_5(out_4), .ce(in_2), .reset(in_3), .ck(clock_1_out));
endmodule

module Registre_8_bit (
  input  [7:0] in_1,
  input  ce,
  input  in_3,
  input  clk,
  output [7:0] s
);

  Registre_1_bit registre_1_bit_1 (.e(in_1[0]), .out_5(s[0]), .ce(ce), .reset(in_3), .ck(clk));
  Registre_1_bit registre_1_bit_2 (.e(in_1[1]), .out_5(s[1]), .ce(ce), .reset(in_3), .ck(clk));
  Registre_1_bit registre_1_bit_3 (.e(in_1[2]), .out_5(s[2]), .ce(ce), .reset(in_3), .ck(clk));
  Registre_1_bit registre_1_bit_4 (.e(in_1[3]), .out_5(s[3]), .ce(ce), .reset(in_3), .ck(clk));
  Registre_1_bit registre_1_bit_5 (.e(in_1[4]), .out_5(s[4]), .ce(ce), .reset(in_3), .ck(clk));
  Registre_1_bit registre_1_bit_6 (.e(in_1[5]), .out_5(s[5]), .ce(ce), .reset(in_3), .ck(clk));
  Registre_1_bit registre_1_bit_7 (.e(in_1[6]), .out_5(s[6]), .ce(ce), .reset(in_3), .ck(clk));
  Registre_1_bit registre_1_bit_8 (.e(in_1[7]), .out_5(s[7]), .ce(ce), .reset(in_3), .ck(clk));
endmodule

module Compteur (
  input  [7:0] in_1,
  input  in_2,
  input  in_3,
  input  in_4,
  output out_5,
  output [7:0] out_6
);

  wire clock_1_out;
  wire [7:0] n8_bit_adder_1_sb0;

  _8_bit_adder u_8_bit_adder_1 (
    .C_in(in_2), .C_out(out_5), .Ab0(out_6[0]), .Ab1(out_6[1]), .Ab2(out_6[2]), .Ab3(out_6[3]),
    .Ab4(out_6[4]), .Ab5(out_6[5]), .Ab6(out_6[6]), .Ab7(out_6[7]), .Bb0(in_1[0]),
    .Sb0(n8_bit_adder_1_sb0[0]), .Bb1(in_1[1]), .Sb1(n8_bit_adder_1_sb0[1]), .Bb2(in_1[2]),
    .Sb2(n8_bit_adder_1_sb0[2]), .Bb3(in_1[3]), .Sb3(n8_bit_adder_1_sb0[3]), .Bb4(in_1[4]),
    .Sb4(n8_bit_adder_1_sb0[4]), .Bb5(in_1[5]), .Sb5(n8_bit_adder_1_sb0[5]), .Bb6(in_1[6]),
    .Sb6(n8_bit_adder_1_sb0[6]), .Bb7(in_1[7]), .Sb7(n8_bit_adder_1_sb0[7]));
  Clock clock_1 (.out(clock_1_out));
  Registre_8_bit registre_8_bit_1 (.in_1(n8_bit_adder_1_sb0), .ce(in_3), .in_3(in_4), .s(out_6), .clk(clock_1_out));
endmodule

module _8_Demux_1_bit (
  input  in_1,
  input  [2:0] in_2,
  output s0,
  output s1,
  output s2,
  output s3,
  output s4,
  output s5,
  output s6,
  output s7
);

  wire demultiplexer_1_out0, demultiplexer_1_out1, demultiplexer_2_out0, demultiplexer_2_out1,
       demultiplexer_3_out0, demultiplexer_3_out1;

  Demultiplexer #(.disabled(0), .enable("false")) demultiplexer_1 (
    .out0(demultiplexer_1_out0), .out1(demultiplexer_1_out1), .in(demultiplexer_2_out0), .sel(in_2[1]));
  Demultiplexer #(.disabled(0), .enable("false")) demultiplexer_2 (
    .out0(demultiplexer_2_out0), .out1(demultiplexer_2_out1), .in(in_1), .sel(in_2[2]));
  Demultiplexer #(.disabled(0), .enable("false")) demultiplexer_3 (
    .out0(demultiplexer_3_out0), .out1(demultiplexer_3_out1), .in(demultiplexer_2_out1), .sel(in_2[1]));
  Demultiplexer #(.disabled(0), .enable("false")) demultiplexer_4 (
    .out0(s0), .out1(s1), .in(demultiplexer_1_out0), .sel(in_2[0]));
  Demultiplexer #(.disabled(0), .enable("false")) demultiplexer_5 (
    .out0(s2), .out1(s3), .in(demultiplexer_1_out1), .sel(in_2[0]));
  Demultiplexer #(.disabled(0), .enable("false")) demultiplexer_6 (
    .out0(s4), .out1(s5), .in(demultiplexer_3_out0), .sel(in_2[0]));
  Demultiplexer #(.disabled(0), .enable("false")) demultiplexer_7 (
    .out0(s6), .out1(s7), .in(demultiplexer_3_out1), .sel(in_2[0]));
endmodule

module _8_Mux_1_bit (
  input  _0,
  input  _1,
  input  _2,
  input  _3,
  input  _4,
  input  _5,
  input  _6,
  input  _7,
  input  [2:0] in_9,
  output out_10
);

  wire multiplexer_1_out, multiplexer_2_out, multiplexer_3_out, multiplexer_4_out, multiplexer_5_out,
       multiplexer_7_out;

  Multiplexer #(.disabled(0), .enable("false")) multiplexer_1 (
    .in0(_0), .in1(_1), .out(multiplexer_1_out), .sel(in_9[0]));
  Multiplexer #(.disabled(0), .enable("false")) multiplexer_2 (
    .in0(_2), .in1(_3), .out(multiplexer_2_out), .sel(in_9[0]));
  Multiplexer #(.disabled(0), .enable("false")) multiplexer_3 (
    .in0(_4), .in1(_5), .out(multiplexer_3_out), .sel(in_9[0]));
  Multiplexer #(.disabled(0), .enable("false")) multiplexer_4 (
    .in0(_6), .in1(_7), .out(multiplexer_4_out), .sel(in_9[0]));
  Multiplexer #(.disabled(0), .enable("false")) multiplexer_5 (
    .in0(multiplexer_1_out), .in1(multiplexer_2_out), .out(multiplexer_5_out), .sel(in_9[1]));
  Multiplexer #(.disabled(0), .enable("false")) multiplexer_6 (
    .in0(multiplexer_5_out), .in1(multiplexer_7_out), .out(out_10), .sel(in_9[2]));
  Multiplexer #(.disabled(0), .enable("false")) multiplexer_7 (
    .in0(multiplexer_3_out), .in1(multiplexer_4_out), .out(multiplexer_7_out), .sel(in_9[1]));
endmodule

module Test_mux (
  input  in_1,
  input  [2:0] in_2,
  output out_3
);

  wire n8_demux_1_bit_1_s0, n8_demux_1_bit_1_s1, n8_demux_1_bit_1_s2, n8_demux_1_bit_1_s3,
       n8_demux_1_bit_1_s4, n8_demux_1_bit_1_s5, n8_demux_1_bit_1_s6, n8_demux_1_bit_1_s7;

  _8_Demux_1_bit u_8_demux_1_bit_1 (
    .s0(n8_demux_1_bit_1_s0), .s1(n8_demux_1_bit_1_s1), .s2(n8_demux_1_bit_1_s2), .s3(n8_demux_1_bit_1_s3),
    .s4(n8_demux_1_bit_1_s4), .s5(n8_demux_1_bit_1_s5), .s6(n8_demux_1_bit_1_s6), .s7(n8_demux_1_bit_1_s7),
    .in_2(in_2));  // open: in_1
  _8_Mux_1_bit u_8_mux_1_bit_1 (
    ._0(n8_demux_1_bit_1_s0), ._1(n8_demux_1_bit_1_s1), ._2(n8_demux_1_bit_1_s2), ._3(n8_demux_1_bit_1_s3),
    ._4(n8_demux_1_bit_1_s4), ._5(n8_demux_1_bit_1_s5), ._6(n8_demux_1_bit_1_s6), ._7(n8_demux_1_bit_1_s7),
    .out_10(out_3), .in_9(in_2));
endmodule

module _8_Mux_2_Bit (
  input  [1:0] in_1,
  input  [1:0] in_2,
  input  [1:0] in_3,
  input  [1:0] in_4,
  input  [1:0] in_5,
  input  [1:0] in_6,
  input  [1:0] in_7,
  input  [1:0] in_8,
  input  [2:0] in_9,
  output [1:0] out_10
);

  _8_Mux_1_bit u_8_mux_1_bit_1 (
    ._0(in_1[0]), ._1(in_2[0]), ._2(in_3[0]), ._3(in_4[0]), ._4(in_5[0]), ._5(in_6[0]), ._6(in_7[0]),
    ._7(in_8[0]), .out_10(out_10[0]), .in_9(in_9));
  _8_Mux_1_bit u_8_mux_1_bit_2 (
    ._0(in_1[1]), ._1(in_2[1]), ._2(in_3[1]), ._3(in_4[1]), ._4(in_5[1]), ._5(in_6[1]), ._6(in_7[1]),
    ._7(in_8[1]), .out_10(out_10[1]), .in_9(in_9));
endmodule

module _8_Mux_4_Bit (
  input  [3:0] in_1,
  input  [3:0] in_2,
  input  [3:0] in_3,
  input  [3:0] in_4,
  input  [3:0] in_5,
  input  [3:0] in_6,
  input  [3:0] in_7,
  input  [3:0] in_8,
  input  [2:0] in_9,
  output [3:0] out_10
);

  _8_Mux_2_Bit u_8_mux_2_bit_1 (
    .out_10(out_10[1:0]), .in_1(in_1[1:0]), .in_2(in_2[1:0]), .in_3(in_3[1:0]), .in_4(in_4[1:0]),
    .in_5(in_5[1:0]), .in_6(in_6[1:0]), .in_7(in_7[1:0]), .in_8(in_8[1:0]), .in_9(in_9));
  _8_Mux_2_Bit u_8_mux_2_bit_2 (
    .out_10(out_10[3:2]), .in_1(in_1[3:2]), .in_2(in_2[3:2]), .in_3(in_3[3:2]), .in_4(in_4[3:2]),
    .in_5(in_5[3:2]), .in_6(in_6[3:2]), .in_7(in_7[3:2]), .in_8(in_8[3:2]), .in_9(in_9));
endmodule

module _8_Mux_8_bit (
  input  [7:0] in_1,
  input  [7:0] in_2,
  input  [7:0] in_3,
  input  [7:0] in_4,
  input  [7:0] in_5,
  input  [7:0] in_6,
  input  [7:0] in_7,
  input  [7:0] in_8,
  input  [2:0] in_9,
  output [7:0] out_10
);

  _8_Mux_4_Bit u_8_mux_4_bit_1 (
    .out_10(out_10[3:0]), .in_1(in_1[3:0]), .in_2(in_2[3:0]), .in_3(in_3[3:0]), .in_4(in_4[3:0]),
    .in_5(in_5[3:0]), .in_6(in_6[3:0]), .in_7(in_7[3:0]), .in_8(in_8[3:0]), .in_9(in_9));
  _8_Mux_4_Bit u_8_mux_4_bit_2 (
    .out_10(out_10[7:4]), .in_1(in_1[7:4]), .in_2(in_2[7:4]), .in_3(in_3[7:4]), .in_4(in_4[7:4]),
    .in_5(in_5[7:4]), .in_6(in_6[7:4]), .in_7(in_7[7:4]), .in_8(in_8[7:4]), .in_9(in_9));
endmodule

module _8_Demux_2_bit (
  input  [1:0] in_1,
  input  [2:0] in_2,
  output [1:0] out_3,
  output [1:0] out_4,
  output [1:0] out_5,
  output [1:0] out_6,
  output [1:0] out_7,
  output [1:0] out_8,
  output [1:0] out_9,
  output [1:0] out_10
);

  _8_Demux_1_bit u_8_demux_1_bit_1 (
    .s0(out_3[0]), .s1(out_4[0]), .s2(out_5[0]), .s3(out_6[0]), .s4(out_7[0]), .s5(out_8[0]), .s6(out_9[0]),
    .s7(out_10[0]), .in_2(in_2), .in_1(in_1[0]));
  _8_Demux_1_bit u_8_demux_1_bit_2 (
    .s0(out_3[1]), .s1(out_4[1]), .s2(out_5[1]), .s3(out_6[1]), .s4(out_7[1]), .s5(out_8[1]), .s6(out_9[1]),
    .s7(out_10[1]), .in_2(in_2), .in_1(in_1[1]));
endmodule

module _8_Demux_4_bit (
  input  [3:0] in_1,
  input  [2:0] in_2,
  output [3:0] out_3,
  output [3:0] out_4,
  output [3:0] out_5,
  output [3:0] out_6,
  output [3:0] out_7,
  output [3:0] out_8,
  output [3:0] out_9,
  output [3:0] out_10
);

  _8_Demux_2_bit u_8_demux_2_bit_1 (
    .in_1(in_1[1:0]), .out_3(out_3[1:0]), .out_4(out_4[1:0]), .out_5(out_5[1:0]), .out_6(out_6[1:0]),
    .out_7(out_7[1:0]), .out_8(out_8[1:0]), .out_9(out_9[1:0]), .out_10(out_10[1:0]), .in_2(in_2));
  _8_Demux_2_bit u_8_demux_2_bit_2 (
    .in_1(in_1[3:2]), .out_3(out_3[3:2]), .out_4(out_4[3:2]), .out_5(out_5[3:2]), .out_6(out_6[3:2]),
    .out_7(out_7[3:2]), .out_8(out_8[3:2]), .out_9(out_9[3:2]), .out_10(out_10[3:2]), .in_2(in_2));
endmodule

module _8_Demux_8_Bit (
  input  [7:0] in_1,
  input  [2:0] in_2,
  output [7:0] out_3,
  output [7:0] out_4,
  output [7:0] out_5,
  output [7:0] out_6,
  output [7:0] out_7,
  output [7:0] out_8,
  output [7:0] out_9,
  output [7:0] out_10
);

  _8_Demux_4_bit u_8_demux_4_bit_1 (
    .out_3(out_3[3:0]), .out_4(out_4[3:0]), .out_5(out_5[3:0]), .out_6(out_6[3:0]), .out_7(out_7[3:0]),
    .out_8(out_8[3:0]), .out_9(out_9[3:0]), .out_10(out_10[3:0]), .in_1(in_1[3:0]), .in_2(in_2));
  _8_Demux_4_bit u_8_demux_4_bit_2 (
    .out_3(out_3[7:4]), .out_4(out_4[7:4]), .out_5(out_5[7:4]), .out_6(out_6[7:4]), .out_7(out_7[7:4]),
    .out_8(out_8[7:4]), .out_9(out_9[7:4]), .out_10(out_10[7:4]), .in_1(in_1[7:4]), .in_2(in_2));
endmodule

module Ram_8_8_Bit (
  input  [7:0] e,
  input  [2:0] adrs,
  input  ce,
  input  reset,
  output [7:0] out_5
);

  wire clock_1_out;
  wire [7:0] n8_demux_8_bit_1_out_3, n8_demux_8_bit_1_out_4, n8_demux_8_bit_1_out_5, n8_demux_8_bit_1_out_6,
       n8_demux_8_bit_1_out_7, n8_demux_8_bit_1_out_8, n8_demux_8_bit_1_out_9, n8_demux_8_bit_1_out_10,
       registre_8_bit_1_s, registre_8_bit_2_s, registre_8_bit_3_s, registre_8_bit_4_s, registre_8_bit_5_s,
       registre_8_bit_6_s, registre_8_bit_7_s, registre_8_bit_8_s;

  _8_Demux_8_Bit u_8_demux_8_bit_1 (
    .out_3(n8_demux_8_bit_1_out_3), .out_4(n8_demux_8_bit_1_out_4), .out_5(n8_demux_8_bit_1_out_5),
    .out_6(n8_demux_8_bit_1_out_6), .out_7(n8_demux_8_bit_1_out_7), .out_8(n8_demux_8_bit_1_out_8),
    .out_9(n8_demux_8_bit_1_out_9), .out_10(n8_demux_8_bit_1_out_10), .in_1(e), .in_2(adrs));
  Clock clock_1 (.out(clock_1_out));
  Registre_8_bit registre_8_bit_1 (
    .in_1(n8_demux_8_bit_1_out_3), .ce(ce), .in_3(reset), .s(registre_8_bit_1_s), .clk(clock_1_out));
  Registre_8_bit registre_8_bit_2 (
    .in_1(n8_demux_8_bit_1_out_4), .ce(ce), .in_3(reset), .s(registre_8_bit_2_s), .clk(clock_1_out));
  Registre_8_bit registre_8_bit_3 (
    .in_1(n8_demux_8_bit_1_out_5), .ce(ce), .in_3(reset), .s(registre_8_bit_3_s), .clk(clock_1_out));
  Registre_8_bit registre_8_bit_4 (
    .in_1(n8_demux_8_bit_1_out_6), .ce(ce), .in_3(reset), .s(registre_8_bit_4_s), .clk(clock_1_out));
  Registre_8_bit registre_8_bit_5 (
    .in_1(n8_demux_8_bit_1_out_7), .ce(ce), .in_3(reset), .s(registre_8_bit_5_s), .clk(clock_1_out));
  Registre_8_bit registre_8_bit_6 (
    .in_1(n8_demux_8_bit_1_out_8), .ce(ce), .in_3(reset), .s(registre_8_bit_6_s), .clk(clock_1_out));
  Registre_8_bit registre_8_bit_7 (
    .in_1(n8_demux_8_bit_1_out_9), .ce(ce), .in_3(reset), .s(registre_8_bit_7_s), .clk(clock_1_out));
  Registre_8_bit registre_8_bit_8 (
    .in_1(n8_demux_8_bit_1_out_10), .ce(ce), .in_3(reset), .s(registre_8_bit_8_s), .clk(clock_1_out));
  _8_Mux_8_bit u_8_mux_8_bit_1 (
    .out_10(out_5), .in_1(registre_8_bit_1_s), .in_2(registre_8_bit_2_s), .in_3(registre_8_bit_3_s),
    .in_4(registre_8_bit_4_s), .in_5(registre_8_bit_5_s), .in_6(registre_8_bit_6_s),
    .in_7(registre_8_bit_7_s), .in_8(registre_8_bit_8_s), .in_9(adrs));
endmodule

module _8_Mux_tests (
  input  [7:0] in_1,
  input  [2:0] in_2,
  output [7:0] out_3
);

  wire [7:0] n8_demux_8_bit_1_out_3, n8_demux_8_bit_1_out_4, n8_demux_8_bit_1_out_5, n8_demux_8_bit_1_out_6,
       n8_demux_8_bit_1_out_7, n8_demux_8_bit_1_out_8, n8_demux_8_bit_1_out_9, n8_demux_8_bit_1_out_10;

  _8_Demux_8_Bit u_8_demux_8_bit_1 (
    .out_3(n8_demux_8_bit_1_out_3), .out_4(n8_demux_8_bit_1_out_4), .out_5(n8_demux_8_bit_1_out_5),
    .out_6(n8_demux_8_bit_1_out_6), .out_7(n8_demux_8_bit_1_out_7), .out_8(n8_demux_8_bit_1_out_8),
    .out_9(n8_demux_8_bit_1_out_9), .out_10(n8_demux_8_bit_1_out_10), .in_1(in_1), .in_2(in_2));
  _8_Mux_8_bit u_8_mux_8_bit_1 (
    .out_10(out_3), .in_1(n8_demux_8_bit_1_out_3), .in_2(n8_demux_8_bit_1_out_4),
    .in_3(n8_demux_8_bit_1_out_5), .in_4(n8_demux_8_bit_1_out_6), .in_5(n8_demux_8_bit_1_out_7),
    .in_6(n8_demux_8_bit_1_out_8), .in_7(n8_demux_8_bit_1_out_9), .in_8(n8_demux_8_bit_1_out_10), .in_9(in_2));
endmodule
