// Logisim project TP1.circ as structural Verilog: 4 circuits, main circuit add1bit
// FA
module add1bit (
  input  A,
  input  B,
  input  C_IN,
  output S,
  output C_OUT
);

  wire and_1_out, and_2_out, and_3_out, xor_1_out;

  xor xor_1 (xor_1_out, A, B);
  and and_1 (and_1_out, A, B);
  and and_2 (and_2_out, A, C_IN);
  and and_3 (and_3_out, B, C_IN);
  xor xor_2 (S, xor_1_out, C_IN);
  or or_1 (C_OUT, and_1_out, and_2_out, and_3_out);

  // Notes on the sheet:
  //   Additionneur 1 bit
endmodule

module add8bits (
  input  [7:0] N1,
  input  [7:0] No,
  input  in_3,
  input  [7:0] N1_2,
  output out_5
);

  wire add1bit_2_c_out, add1bit_3_c_out, add1bit_4_c_out, add1bit_5_c_out, add1bit_6_c_out, add1bit_7_c_out,
       add1bit_8_c_out;

  add1bit add1bit_1 (.A(N1[7]), .B(No[7]), .C_IN(add1bit_2_c_out), .S(N1_2[7]), .C_OUT(out_5));
  add1bit add1bit_2 (.A(N1[6]), .B(No[6]), .C_IN(add1bit_3_c_out), .S(N1_2[6]), .C_OUT(add1bit_2_c_out));
  add1bit add1bit_3 (.A(N1[5]), .B(No[5]), .C_IN(add1bit_4_c_out), .S(N1_2[5]), .C_OUT(add1bit_3_c_out));
  add1bit add1bit_4 (.A(N1[4]), .B(No[4]), .C_IN(add1bit_5_c_out), .S(N1_2[4]), .C_OUT(add1bit_4_c_out));
  add1bit add1bit_5 (.A(N1[3]), .B(No[3]), .C_IN(add1bit_6_c_out), .S(N1_2[3]), .C_OUT(add1bit_5_c_out));
  add1bit add1bit_6 (.A(N1[2]), .B(No[2]), .C_IN(add1bit_7_c_out), .S(N1_2[2]), .C_OUT(add1bit_6_c_out));
  add1bit add1bit_7 (.A(N1[1]), .B(No[1]), .C_IN(add1bit_8_c_out), .S(N1_2[1]), .C_OUT(add1bit_7_c_out));
  add1bit add1bit_8 (.A(N1[0]), .B(No[0]), .C_IN(in_3), .S(N1_2[0]), .C_OUT(add1bit_8_c_out));
endmodule

module addorrmv8bits (
  input  C_IN,
  input  [7:0] B,
  input  [7:0] plus_1,
  input  [7:0] _1,
  output [7:0] out_5
);

  wire [7:0] comp_1_out_3, undriven;

  comp comp_1 (.X(B), .C_IN(C_IN), .out_3(comp_1_out_3));
  add8bits add8bits_1 (.in_3(C_IN), .N1(plus_1), .No(comp_1_out_3), .N1_2(undriven));  // open: out_5
  add8bits add8bits_2 (.in_3(C_IN), .N1(_1), .No(undriven), .N1_2(out_5));  // open: out_5
endmodule

module comp (
  input  [7:0] X,
  input  C_IN,
  output [7:0] out_3
);

  xor xor_1 (out_3[0], X[0], C_IN);
  xor xor_2 (out_3[1], X[1], C_IN);
  xor xor_3 (out_3[2], X[2], C_IN);
  xor xor_4 (out_3[3], X[3], C_IN);
  xor xor_5 (out_3[4], X[4], C_IN);
  xor xor_6 (out_3[5], X[5], C_IN);
  xor xor_7 (out_3[6], X[6], C_IN);
  xor xor_8 (out_3[7], X[7], C_IN);
endmodule
